# Fritzing sketch pico_pir_sensor (saved by Fritzing 0.9.3b)
breadboards: 1

parts:
  PIR1 = PIR sensor
  Mod1 = Raspberry Pi Pico

nets:
  N1: PIR1.VDD, Mod1.pin_36
  N2: PIR1.SIG, Mod1.pin_21
  N3: PIR1.GND, Mod1.pin_23

custom parts:
  Raspberry Pi Pico: Raspberry Pi Pico. Based around the RP2040 microcontroller the Pico is a low cost microcontroller device bringing Raspberry Pi quality, cost, and easy of use to the microcontroller space. Jan 2021, Split part in to two versions: tht (this one) and SMD. This one will drill holes for a .1 in header in pcb to allow plugging in the module as well as providing pads to solder the module to the top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

// code stored in the sketch: pir_sensor.ino
/* The sensor's output pin goes to HIGH if motion is present.
 * However, even if motion is present, it goes to LOW from time to time, 
 * which might give the impression no motion is present. 
 * This program deals with this issue by ignoring LOW-phases shorter than a given time, 
 * assuming continuous motion is present during these phases.
 *  
 */

/////////////////////////////
//VARS
int calibrationTime = 30; //the time we give the sensor to calibrate (10-60 secs according to the datasheet)       
long unsigned int lowIn;  //the time when the sensor outputs a low impulse
long unsigned int pause = 5000;  //the amount of milliseconds the sensor has to be low before we assume all motion has stopped

boolean lockLow = true;
boolean takeLowTime;  

int pirPin = 2;    //the digital pin connected to the PIR sensor's output
//int ledPin = 13;


/////////////////////////////
//SETUP
void setup(){
  Serial.begin(9600);
  pinMode(pirPin, INPUT);
  //pinMode(ledPin, OUTPUT);
  digitalWrite(pirPin, LOW); //No movement at the beginning

  //give the sensor some time to calibrate
  Serial.print("calibrating sensor ");
    for(int i = 0; i < calibrationTime; i++){
      Serial.print(".");
      delay(1000);
      }
    Serial.println(" done");
    Serial.println("SENSOR ACTIVE");
    delay(50);
  }

////////////////////////////
//LOOP
void loop(){

  if(digitalRead(pirPin) == HIGH){
      //digitalWrite(ledPin, HIGH);   //the led visualizes the sensors output pin state
      if(lockLow){  
         //makes sure we wait for a transition to LOW before any further output is made:
         lockLow = false;            
         Serial.println("---");
         Serial.print("motion detected at ");
         Serial.print(millis()/1000);
         Serial.println(" sec"); 
         delay(50);
         }         
       takeLowTime = true;
  }

  if(digitalRead(pirPin) == LOW){       
       //digitalWrite(ledPin, LOW);  //the led visualizes the sensors output pin state
       if(takeLowTime){
          lowIn = millis();          //save the time of the transition from high to LOW
          takeLowTime = false;       //make sure this is only done at the start of a LOW phase
       }
       //if the sensor is low for more than the given pause, 
       //we assume that no more motion is going to happen
       if(!lockLow && millis() - lowIn > pause){  
           //makes sure this block of code is only executed again after 
           //a new motion sequence has been detected
           lockLow = true;                        
           Serial.print("motion ended at ");      //output
           Serial.print((millis() - pause)/1000);
           Serial.println(" sec");
           delay(50);
       }
  }
}
